// Logisim project COA_final_project_1.circ as structural Verilog
module main (
  input  a,
  input  b,
  input  c,
  output y
);

  wire nand_1_out, nand_2_out, nand_3_out;

  nand nand_1 (nand_1_out, 1'b1, b);
  nand nand_2 (nand_2_out, 1'b1, c);
  nand nand_3 (nand_3_out, a, nand_1_out);
  // NOR_Gate nor_1 is placed but not wired
  nand nand_4 (y, nand_2_out, nand_3_out);
endmodule

module register16bit (
  input  [15:0] Data,
  input  WE,
  input  Clk,
  input  Reset,
  input  OE,
  output [15:0] Result,
  output [15:0] Dout,
  output [7:0] Eight_LSBs,
  output [7:0] Eight_MSBs
);

  Register #(.width(16)) register_1 (.D(Data), .en(WE), .clk(Clk), .Q(Result), .clr(Reset));
  assign Dout = OE ? Result : 16'bz;  // Controlled_Buffer controlled_buffer_1
  BitSelector #(.group(8), .width(16)) bitselector_1 (.in(Dout), .out(Eight_MSBs), .sel(1'b1));
  BitSelector #(.group(8), .width(16)) bitselector_2 (.in(Dout), .out(Eight_LSBs), .sel(1'b0));
endmodule

module register8bits (
  input  [15:0] Data,
  input  WE,
  input  Clk,
  input  Reset,
  output [15:0] Result
);

  Register #(.width(16)) register_1 (.D(Data), .en(WE), .clk(Clk), .Q(Result), .clr(Reset));
endmodule

module datapath (
);

  register16bit Register_A ();  // open: Data, WE, Clk, Reset, OE, Result, Dout, Eight_LSBs, Eight_MSBs
  register16bit Register_B ();  // open: Data, WE, Clk, Reset, OE, Result, Dout, Eight_LSBs, Eight_MSBs
  register16bit Output_register ();  // open: Data, WE, Clk, Reset, OE, Result, Dout, Eight_LSBs, Eight_MSBs
  register16bit Intruction_register ();  // open: Data, WE, Clk, Reset, OE, Result, Dout, Eight_LSBs, Eight_MSBs
endmodule
